# Fritzing sketch Sketch 1 (saved by Fritzing 0.9.3b)
breadboards: 1

parts:
  DHT1 = Humidity and Temperature Sensor DHT11
  WATER_PUMP1 = water pump/motor
  U2 = ESP8266 NodeMCU LoLin module
  Mod1 = KY-019 5V Relay Module [package="Breakout board"]
  元件1 = SPI OLED Monochrome 128x64 0.96 inch
  Capacitive_Soil_Moisture_Sensor1 = DFRobot Capacitive Soil Moisture Sensor V1.0 [part_number=SEN0193]
  U3 = LIPO-2000mAh [package=lipo-2000]

nets:
  VCC: DHT1.Vcc, U2.3V3, Mod1.+, Mod1.Common, 元件1.VDD, U3.+
  N1: DHT1.Data-signal, U2.D8
  GND: DHT1.GND_2, WATER_PUMP1.pin_1, WATER_PUMP1.pin_2, U2.GND, Mod1.-, Mod1.NO, 元件1.GND, Capacitive_Soil_Moisture_Sensor1.GND, U3.-
  N2: U2.D2, Mod1.S
  N3: U2.D3, 元件1.DC
  N4: U2.D4, 元件1.RES
  N5: U2.D5, 元件1.SCK
  N6: U2.D6, 元件1.SDA
  N7: U2.D7, 元件1.CS
  N8: U2.VU, Capacitive_Soil_Moisture_Sensor1.VCC
  N9: U2.A0, Capacitive_Soil_Moisture_Sensor1.A

custom parts:
  Humidity and Temperature Sensor DHT11: Digital relative humidity & temperature sensor DHT11
  water pump/motor: WATER PUMP BY ARDUBLOCKTR
  ESP8266 NodeMCU LoLin module: ESP8266 based NodeMCU
  KY-019 5V Relay Module: KY-019 5V Relay module, used to control AC circuits.
  SPI OLED Monochrome 128x64 0.96 inch: Unknown 128x64 0.96 inch 128x64 SPI Monochrome OLED display
  DFRobot Capacitive Soil Moisture Sensor V1.0: DFRobot Capacitive Soil Moisture Sensor V1.0 This product measures soil moisture levels by capacitive sensing, rather than resistive sensing like other types of moisture sensor. It is made of a corrosion resistant material giving it a long service life. Insert it into soil and impress your friends with the real-time soil moisture data! The product includes an on-board voltage regulator which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
